// Logisim project Counter.circ as structural Verilog: 1 circuit, main circuit main
module main (
);

  wire button_1_out, t_ff_1_q, t_ff_2_q, t_ff_3_q;
  wire [2:0] not_1_out;

  Button button_1 (.out(button_1_out));
  not not_1 (not_1_out[0], t_ff_1_q);
  T_Flip_Flop t_ff_1 (.clk(button_1_out), .T(1'b1), .Q(t_ff_1_q));  // open: Qn, preset, reset
  T_Flip_Flop t_ff_2 (.clk(t_ff_1_q), .T(1'b1), .Q(t_ff_2_q));  // open: Qn, preset, reset
  // Probe on not_1_out
  not not_2 (not_1_out[1], t_ff_2_q);
  T_Flip_Flop t_ff_3 (.clk(t_ff_2_q), .T(1'b1), .Q(t_ff_3_q));  // open: Qn, preset, reset
  not not_3 (not_1_out[2], t_ff_3_q);
endmodule
